# Fritzing sketch HumidifierController (saved by Fritzing 0.9.2b)
circuit board: 9.21968cm x 5.69638cm
breadboards: 1

parts:
  Part2 = Arduino Nano (Rev3.0)
  Q1 = NPN-Transistor [package="TO92 [THT]"]
  R1 = Resistor [tolerance=±5% resistance=22k package="0805 [SMD]"]
  R2 = Resistor [tolerance=±5% resistance=680 package="0805 [SMD]"]
  R3 = Resistor [tolerance=±5% resistance=220 package="0805 [SMD]"]
  C1 = Electrolytic Capacitor [capacitance=47µF voltage=50V package="0405 [SMD, electrolytic]"]
  D2 = Diode [package=diode-1n4001]
  D3 = Zener Diode [part_number=1N5249B package="300 mil [THT]"]
  F1 = FUSE [package=fuse_5mm]
  JP1 = Header 3 [package=screwterminal-3.5mm-3_lock.007s]
  D1 = Diode [package=diode-1n4001]
  JP2 = Header 4 [package=screwterminal-3.5mm-4_lock]

nets:
  N1: Part2.GND, Q1.C, R2.Pin_0, R2.Pin_1, C1.-, D2.A, D3.anode, JP1.2, JP2.2
  N2: Part2.D2, R1.Pin_0
  N3: Part2.D10, JP2.3
  N4: Part2.D11/MOSI, JP2.4
  N5: Part2.VIN, C1.+, D3.cathode, F1.1
  N6: Part2.5V, JP2.1
  N7: Q1.E, R3.Pin_1
  N8: Q1.B, R1.Pin_1
  N9: R3.Pin_0, D2.C, JP1.1
  N10: F1.2, D1.C
  N11: JP1.3, D1.A

custom parts:
  Zener Diode: A standard zener diode
